// Logisim project HC_circuit.circ as structural Verilog: 1 circuit, main circuit main
module main (
  input  in_1,
  input  in_2,
  input  in_3,
  output [3:0] out_4,
  output [3:0] out_5,
  output [3:0] out_6,
  output [3:0] out_7,
  output [3:0] out_8
);

  wire _0_out, _1_out, _2_out, _3_out, _4_out, _5_out, _6_out, _7_out, _8_out, _9_out, _10_out, _11_out,
       _12_out, _13_out, _14_out, _15_out, not_2_out, not_3_out, not_4_out, not_5_out, not_6_out, not_7_out,
       not_8_out, not_9_out, not_10_out, not_11_out, or_1_out, or_2_out, or_3_out, or_4_out, xor_1_out,
       xor_2_out, xor_3_out, xor_4_out, xor_5_out, xor_6_out, xor_7_out, xor_8_out;
  wire [2:2] not_1_out;

  Button _0 (.out(_0_out));
  Button _3 (.out(_3_out));
  Button _6 (.out(_6_out));
  Button _9 (.out(_9_out));
  Button _11 (.out(_11_out));
  Button _13 (.out(_13_out));
  Button _15 (.out(_15_out));
  Button _1 (.out(_1_out));
  Button _4 (.out(_4_out));
  Button _7 (.out(_7_out));
  Button _10 (.out(_10_out));
  Button _12 (.out(_12_out));
  Button _14 (.out(_14_out));
  Button _5 (.out(_5_out));
  Button _8 (.out(_8_out));
  Button _2 (.out(_2_out));
  Priority_Encoder #(.select(4)) priority_encoder_1 (
    .in0(_0_out), .in1(_1_out), .in2(_2_out), .in3(_3_out), .in4(_4_out), .in5(_5_out), .in6(_6_out),
    .in7(_7_out), .in8(_8_out), .in9(_9_out), .in10(_10_out), .in11(_11_out), .in12(_12_out), .in13(_13_out),
    .in14(_14_out), .in15(_15_out), .out(out_7));  // open: gs, en_out, en_in
  Hex_Digit_Display hex_digit_display_1 (.value(out_7));  // open: dp
  xor xor_1 (xor_1_out, out_7[2], out_7[3]);
  not not_1 (not_1_out[2], out_7[2]);
  xor xor_2 (xor_2_out, out_7[0], out_7[1]);
  xor r0 (out_4[0], xor_2_out, out_7[3]);
  xor r1 (out_4[1], out_7[0], xor_1_out);
  xor r2 (out_4[2], out_7[1], xor_1_out);
  Hex_Digit_Display hex_digit_display_2 (.value({out_7[3], not_1_out[2], out_7[1:0]}));  // open: dp
  Hex_Digit_Display hex_digit_display_3 (.value({in_3, out_4[2:0]}));  // open: dp
  xor xor_3 (xor_3_out, out_7[1], not_1_out[2]);
  Hex_Digit_Display hex_digit_display_4 (.value({in_1, out_4[2:0]}));  // open: dp
  xor xor_4 (xor_4_out, out_7[0], out_7[1]);
  xor xor_5 (xor_5_out, not_1_out[2], out_7[3]);
  Hex_Digit_Display hex_digit_display_5 (.value({in_2, out_5[2:0]}));  // open: dp
  xor xor_6 (xor_6_out, xor_4_out, out_7[3]);
  xor xor_7 (xor_7_out, xor_5_out, out_7[0]);
  xor xor_8 (xor_8_out, xor_3_out, out_7[3]);
  xor _3_2 (out_5[2], xor_6_out, out_4[0]);
  xor _2_2 (out_5[1], xor_7_out, out_4[1]);
  xor _1_2 (out_5[0], xor_8_out, out_4[2]);
  not not_2 (not_2_out, out_5[2]);
  not not_3 (not_3_out, out_5[1]);
  not not_4 (not_4_out, out_5[0]);
  not not_5 (not_5_out, out_5[1]);
  not not_6 (not_6_out, out_5[0]);
  not not_7 (not_7_out, out_5[2]);
  not not_8 (not_8_out, out_5[0]);
  not not_9 (not_9_out, out_5[2]);
  not not_10 (not_10_out, out_5[1]);
  not not_11 (not_11_out, out_5[0]);
  or or_1 (or_1_out, not_2_out, not_3_out, not_4_out);
  or or_2 (or_2_out, out_5[2], not_5_out, not_6_out);
  or or_3 (or_3_out, out_5[1], not_7_out, not_8_out);
  or or_4 (or_4_out, not_9_out, not_10_out, not_11_out);
  xnor xnor_1 (out_6[3], or_1_out, out_7[3]);
  xnor xnor_2 (out_6[2], not_1_out[2], or_2_out);
  xnor xnor_3 (out_6[1], out_7[1], or_3_out);
  xnor xnor_4 (out_6[0], out_7[0], or_4_out);
  Hex_Digit_Display hex_digit_display_6 (.value(out_6));  // open: dp

  assign out_4[3] = in_1;
  assign out_5[3] = in_2;
  assign out_8 = {in_3, out_4[2:0]};

  // Notes on the sheet:
  //   a3 a2 a1 a0
  //   encoder
  //   r2 r1 r0
  //   b3b2b1b0
  //   q2q1q0
  //   checker
  //   decoder
  //   s2s1s0 
  //   correct
  //   final a3a2a1a0
endmodule
